# Fritzing sketch scout_midi_out (saved by Fritzing 0.9.4)

parts:
  Scout_UART = Header 6 [package=1x06_smd_straight_alt]
  Part1 = Adafruit QT Py RP2040 [part_number="Adafruit #4900"]

nets:
  N1: Scout_UART.2, Part1.RX
  N2: Scout_UART.4, Part1.+5V
  N3: Scout_UART.6, Part1.GND

notes:
  GND is pin 1 on the Scout's output pins. Please refer to Scout schematic for full detail.

custom parts:
  Adafruit QT Py RP2040: Description What a cutie pie! Or is it... a QT Py? This diminutive dev board comes with one of our new favorite chip, the RP2040. It's been made famous in the new Raspberry Pi Pico and our Feather RP2040 and ItsyBitsy RP2040, but what if we wanted something really smol? A new chip means a new QT Py, and the Raspberry Pi RP2040 is no exception. When we saw this chip we thought "this chip is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
